// Logisim project D8421.circ as structural Verilog: 1 circuit, main circuit main
module main (
  input  [3:0] in_1,
  output [3:0] out_2
);

  wire and_1_out, not_2_out, not_3_out, not_4_out, or_1_out, or_2_out, or_3_out;

  not not_1 (out_2[0], in_1[0]);
  not not_2 (not_2_out, in_1[0]);
  not not_3 (not_3_out, in_1[1]);
  not not_4 (not_4_out, in_1[2]);
  xor xor_1 (out_2[1], in_1[0], in_1[1]);
  or or_1 (or_1_out, in_1[0], in_1[2]);
  or or_2 (or_2_out, in_1[1], in_1[2]);
  or or_3 (or_3_out, not_2_out, not_3_out, not_4_out);
  and and_1 (and_1_out, in_1[0], in_1[1], in_1[2]);
  and and_2 (out_2[2], or_1_out, or_2_out, or_3_out);
  or or_4 (out_2[3], and_1_out, in_1[3]);

  // Notes on the sheet:
  //   Y1
  //   Y2
endmodule
